# Fritzing sketch esp somfy rf_v1.2 (saved by Fritzing 0.9.3b)
circuit board: 6.17872cm x 4.52976cm
breadboards: 2

parts:
  esp8266_Lolin = NodeMCU V3.0
  LED = LED - 5mm [color="Red (633nm)" package="5 mm [THT]"]
  fs1000a = FS1000A - 433Mhz RF Transmitter [package=THT]

nets:
  N1: esp8266_Lolin.D1, LED.anode, fs1000a.DATA
  GND: esp8266_Lolin.GND, LED.cathode, fs1000a.GND
  N2: esp8266_Lolin.VU, fs1000a.VCC

notes:
  esp somfy rf v1.0
  NodeMCU v3
  433.24Mhz

custom parts:
  NodeMCU V3.0: ESP8266 based NodeMCU
  FS1000A - 433Mhz RF Transmitter: This is 433Mhz RF transmitter with receiver kit for Arduino ARM MCU wireless Application environment: Remote control switch, receiver module, motorcycles, automobile anti-theft products, home security products, electric doors, shutter doors, windows, remote control socket, remote control LED, remote audio remote control electric doors, garage door remote control, remote control retractable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
